# Fritzing sketch partA (saved by Fritzing 0.9.10b)
breadboards: 1

parts:
  U1 = 7400 4 x 2 Input NAND Gate [part_number=7400 package="DIP (Dual Inline) [THT]"]

nets:
  A (input): U1.A1
  B (select): U1.B1, U1.Q2, U1.A2
  N1: U1.Q1, U1.A4
  N2: U1.B2, U1.B3
  GND: U1.GND
  N3: U1.A3, U1.B4
  C (input): U1.Q3
  Z (output): U1.Q4
  3.3V: U1.VDD
