# Fritzing sketch partB (saved by Fritzing 0.9.10b)
breadboards: 1

parts:
  U1 = 7400 4 x 2 Input NAND Gate [part_number=7400 package="DIP (Dual Inline) [THT]"]
  U2 = 7400 4 x 2 Input NAND Gate [part_number=7400 package="DIP (Dual Inline) [THT]"]

nets:
  A (input): U1.A1, U2.B1
  B (select): U1.B1, U1.Q2, U1.A2
  N1: U1.Q1, U1.A4
  N2: U1.B2, U1.B3
  GND: U1.GND, U2.GND
  N3: U1.A3, U1.B4
  C (input): U1.Q3, U2.A1
  N4: U1.Q4, U2.A4, U2.B4
  3.3V/5V: U1.VDD, U2.VDD
  N5: U2.Q1, U2.Q2
  N6: U2.A2, U2.Q4
  net label: U2.B2

notes:
  A (input)
  B (select)
  C (input)
  Z (output)
