# Fritzing sketch breadboard (saved by Fritzing 0.9.10b)
breadboards: 3

parts:
  U1 = 74194 4 Bit Bi-Directional Shift Register [part_number=74194 package="DIP16 [THT]"]
  U2 = 74194 4 Bit Bi-Directional Shift Register [part_number=74194 package="DIP16 [THT]"]
  U3 = 7400 4 x 2 Input NAND Gate [part_number=7400 package="DIP (Dual Inline) [THT]"]
  U4 = 7402 4 x 2 Input NOR Gate [part_number=7402 package="DIP (Dual Inline) [THT]"]
  U5 = 7486 4 x 2 Input XOR Gate [part_number=7486 package="DIP (Dual Inline) [THT]"]
  U6 = 7404 Hex Inverter [part_number=7404 package=dil14]
  U7 = 74151 8:1 MUX [part_number=74151 package="DIP16 [THT]"]
  U8 = 74153 Dual 4:1 MUX [part_number=74153 package="DIP16 [THT]"]
  U9 = 7474 Dual Positive Edge Triggered D Flip Flop [part_number=7474 package="DIP (Dual Inline) [THT]"]
  U10 = 74161 4 Bit Synchronous Up Down Counter [part_number=74161 package="DIP16 [THT]"]
  U11 = 7427 3 x 3 Input NOR Gate [part_number=7427 package="DIP (Dual Inline) [THT]"]
  U12 = 7404 Hex Inverter [part_number=7404 package=dil14]

nets:
  VCC: U1.1, U1.VCC, U2.1, U2.VCC, U3.VDD, U4.VDD, U5.VDD, U6.VCC, U7.1, U7.VCC, U8.VCC, U9.A1, U9.Q2, U9.VDD, U10.7, U10.10, U10.VCC, U11.VDD, U12.VCC
  N1: U1.2, U8.Y0
  N2: U1.3, U2.3
  N3: U1.4, U2.4
  N4: U1.5, U2.5
  N5: U1.6, U2.6
  N6: U1.9, U6.6Y
  N7: U1.10, U4.A4
  N8: U1.12, U3.A1, U4.B1, U5.A1, U8.A0, U8.B0, U8.D1
  N9: U2.2, U8.Y1
  N10: U2.9, U6.5Y
  N11: U2.10, U4.B3
  N12: U2.12, U3.B1, U4.Q1, U5.B1, U8.D0, U8.C1, U8.A1
  N13: U3.Q1, U6.1A, U7.15
  GND: U3.GND, U4.B2, U5.GND, U6.GND, U7.7, U7.GND, U7.12, U8.G1, U8.G0, U8.GND, U9.GND, U10.GND, U11.GND, U12.GND
  N14: U3.Q4, U6.4A
  N15: U3.A4, U9.B2
  N16: U3.B4, U12.3A
  N17: U4.A1, U6.2A, U7.14
  N18: U4.Q3, U6.5A
  N19: U4.Q4, U5.A3, U10.1, U11.A4
  N20: U4.B4, U6.6A
  N21: U5.Q1, U6.3A, U7.13
  N22: U6.1Y, U7.2
  N23: U6.2Y, U7.3
  N24: U6.3Y, U7.4
  N25: U6.4Y, U12.6A
  N26: U7.5, U8.C0, U8.B1
  N27: U9.B1, U11.B1
  N28: U10.13, U12.1Y, U12.2Y
  N29: U10.14, U12.1A, U12.2A
  N30: U11.A1, U12.3Y
  N31: U11.B4, U12.6Y

notes:
  F0
  F1
  F2
  Execute
  LOAD B
  LOAD A
  R0
  R1
  Din0
  Din1
  Din2
  Din3

custom parts:
  7404 Hex Inverter: 74XX04 Hex Inverter, Modified by Zuofu Cheng (Aug 2020)
  74151 8:1 MUX: 74151 8:1 Multiplexor
  74153 Dual 4:1 MUX: 74153 Dual 4:1 Multiplexor
  7427 3 x 3 Input NOR Gate: 7427 3 x 2 Input NOR Gate
