# Fritzing sketch computation unit (saved by Fritzing 0.9.10b)
breadboards: 1

parts:
  U1 = 74151 8:1 MUX [part_number=74151 package="DIP16 [THT]"]
  NAND = 7400 4 x 2 Input NAND Gate [part_number=7400 package="DIP (Dual Inline) [THT]"]
  NOR = 7402 4 x 2 Input NOR Gate [part_number=7402 package="DIP (Dual Inline) [THT]"]
  XOR = 7486 4 x 2 Input XOR Gate [part_number=7486 package="DIP (Dual Inline) [THT]"]
  U5 = 7404 Hex Inverter [part_number=7404 package=dil14]

nets:
  3.3V: U1.1, U1.VCC, NAND.VDD, NOR.VDD, XOR.VDD, U5.VCC
  N1: U1.2, XOR.Q1, U5.3A
  N2: U1.3, U5.2Y
  N3: U1.4, U5.1Y
  F(A,B): U1.5
  GND: U1.7, U1.GND, U1.12, NAND.GND, NOR.GND, XOR.GND, U5.GND
  F2: U1.9
  F1: U1.10
  F0: U1.11
  N4: U1.13, U5.3Y
  N5: U1.14, NOR.A1, U5.2A
  N6: U1.15, NAND.Q1, U5.1A
  A: NAND.A1, NOR.B1, XOR.A1
  B: NAND.B1, NOR.Q1, XOR.B1

custom parts:
  74151 8:1 MUX: 74151 8:1 Multiplexor
  7404 Hex Inverter: 74XX04 Hex Inverter, Modified by Zuofu Cheng (Aug 2020)
