# Fritzing sketch control unit (saved by Fritzing 0.9.10b)
breadboards: 1

parts:
  FF = 7474 Dual Positive Edge Triggered D Flip Flop [part_number=7474 package="DIP (Dual Inline) [THT]"]
  Counter = 74161 4 Bit Synchronous Up Down Counter [part_number=74161 package="DIP16 [THT]"]
  NAND = 7400 4 x 2 Input NAND Gate [part_number=7400 package="DIP (Dual Inline) [THT]"]
  NOT = 7404 Hex Inverter [part_number=7404 package=dil14]
  NOR = 7427 3 x 3 Input NOR Gate [part_number=7427 package="DIP (Dual Inline) [THT]"]

nets:
  3.3V: FF.A1, FF.Q2, FF.VDD, Counter.7, Counter.9, Counter.10, Counter.VCC, NAND.VDD, NOT.VCC, NOR.VDD
  Q+: FF.B1
  Clk: FF.Q1, Counter.2
  Q: FF.A2
  Q': FF.B2, NAND.B1
  GND: FF.GND, Counter.GND, NAND.GND, NOT.GND, NOR.GND
  S: Counter.1, NOR.B2
  C1: Counter.13, NOR.B1, NOR.Q2
  C0: Counter.14, NOR.A1, NOR.Q1
  E: NAND.A1, NOR.B4
  (EQ')': NAND.Q1, NOT.1A
  Q'E: NOT.1Y
  EQ': NOR.A2
  Q+|: NOR.A4

custom parts:
  7404 Hex Inverter: 74XX04 Hex Inverter, Modified by Zuofu Cheng (Aug 2020)
  7427 3 x 3 Input NOR Gate: 7427 3 x 2 Input NOR Gate
