# Fritzing sketch register unit (saved by Fritzing 0.9.10b)
breadboards: 3

parts:
  RegA = 74194 4 Bit Bi-Directional Shift Register [part_number=74194 package="DIP16 [THT]"]
  RegB = 74194 4 Bit Bi-Directional Shift Register [part_number=74194 package="DIP16 [THT]"]
  NOR = 7402 4 x 2 Input NOR Gate [part_number=7402 package="DIP (Dual Inline) [THT]"]
  NOT = 7404 Hex Inverter [part_number=7404 package=dil14]

nets:
  3.3V: RegA.1, RegA.VCC, RegB.1, RegB.VCC, NOT.VCC
  A+: RegA.2
  D0: RegA.3, RegB.3
  D1: RegA.4, RegB.4
  D2: RegA.5, RegB.5
  D3: RegA.6, RegB.6
  GND: RegA.GND, RegB.GND, NOR.GND, NOT.GND
  N1: RegA.9, NOT.1Y
  load A: RegA.10, NOR.B1
  Clk: RegA.11, RegB.11
  A3: RegA.12
  A2: RegA.13
  A1: RegA.14
  A0: RegA.15
  B+: RegB.2
  N2: RegB.9, NOT.2Y
  load B: RegB.10, NOR.B2
  B3: RegB.12
  B2: RegB.13
  B1: RegB.14
  B0: RegB.15
  N3: NOR.A1, NOT.1A
  Shift (control): NOR.Q1, NOR.A2
  N4: NOR.Q2, NOT.2A

custom parts:
  7404 Hex Inverter: 74XX04 Hex Inverter, Modified by Zuofu Cheng (Aug 2020)
