# Fritzing sketch routing unit (saved by Fritzing 0.9.10b)
breadboards: 1

parts:
  4_1MUX = 74153 Dual 4:1 MUX [part_number=74153 package="DIP16 [THT]"]
  4_1MUX_2 = 74153 Dual 4:1 MUX [part_number=74153 package="DIP16 [THT]"]

nets:
  B: 4_1MUX.D0, 4_1MUX_2.C0, 4_1MUX_2.A0
  F: 4_1MUX.C0, 4_1MUX_2.B0
  A+: 4_1MUX.Y0
  GND: 4_1MUX.GND, 4_1MUX_2.GND
  R1: 4_1MUX.S1, 4_1MUX_2.S1
  A: 4_1MUX.A0, 4_1MUX.B0, 4_1MUX_2.D0
  R0: 4_1MUX.S0, 4_1MUX_2.S0
  3.3V: 4_1MUX.VCC, 4_1MUX_2.VCC
  B+: 4_1MUX_2.Y0

custom parts:
  74153 Dual 4:1 MUX: 74153 Dual 4:1 Multiplexor
